// Logisim project hw1.circ as structural Verilog: 5 circuits, main circuit reptile8
// Register Bank
module reg_bank (
  input  clk,
  input  [15:0] Din,
  input  LD,
  input  [2:0] regsel,
  output [15:0] Dout0,
  output [15:0] Dout1,
  output [15:0] Dout2,
  output [15:0] Dout3,
  output [15:0] Dout4,
  output [15:0] Dout5,
  output [15:0] Dout6,
  output [15:0] Dout7
);

  wire and_1_out, and_2_out, and_3_out, and_4_out, and_5_out, and_6_out, and_7_out, and_8_out,
       decoder_1_out0, decoder_1_out1, decoder_1_out2, decoder_1_out3, decoder_1_out4, decoder_1_out5,
       decoder_1_out6, decoder_1_out7;

  and and_1 (and_1_out, decoder_1_out0, LD);
  and and_2 (and_2_out, decoder_1_out1, LD);
  and and_3 (and_3_out, decoder_1_out2, LD);
  and and_4 (and_4_out, decoder_1_out4, LD);
  and and_5 (and_5_out, decoder_1_out3, LD);
  Decoder #(.select(3), .enable("false")) decoder_1 (
    .out0(decoder_1_out0), .out1(decoder_1_out1), .out2(decoder_1_out2), .out3(decoder_1_out3),
    .out4(decoder_1_out4), .out5(decoder_1_out5), .out6(decoder_1_out6), .out7(decoder_1_out7), .sel(regsel));
  and and_6 (and_6_out, decoder_1_out5, LD);
  and and_7 (and_7_out, decoder_1_out6, LD);
  and and_8 (and_8_out, decoder_1_out7, LD);
  Register #(.width(16)) register_1 (.D(Din), .en(and_1_out), .Q(Dout0), .clk(clk));  // open: clr
  Register #(.width(16)) register_2 (.D(Din), .en(and_2_out), .Q(Dout1), .clk(clk));  // open: clr
  Register #(.width(16)) register_3 (.D(Din), .en(and_3_out), .Q(Dout2), .clk(clk));  // open: clr
  Register #(.width(16)) register_4 (.D(Din), .en(and_5_out), .Q(Dout3), .clk(clk));  // open: clr
  Register #(.width(16)) register_5 (.D(Din), .en(and_4_out), .Q(Dout4), .clk(clk));  // open: clr
  Register #(.width(16)) register_6 (.D(Din), .en(and_6_out), .Q(Dout5), .clk(clk));  // open: clr
  Register #(.width(16)) register_7 (.D(Din), .en(and_7_out), .Q(Dout6), .clk(clk));  // open: clr
  Register #(.width(16)) register_8 (.D(Din), .en(and_8_out), .Q(Dout7), .clk(clk));  // open: clr
endmodule

module reptile8 (
);

  wire alu_rep8_1_zero_flag, ARMUX, clk, IRLD, MEMLD, MUX, PCINC, PCLD, REGLD, ZF, ZFLD;
  wire [2:0] opcode;
  wire [5:0] ALUOP, offset;
  wire [11:0] adder_1_out, address, mem_addr, pc_reg_1_dout;
  wire [15:0] alu_rep8_1_res, Din, Dout, reg_bank_1_dout0, reg_bank_1_dout1, reg_bank_1_dout2,
       reg_bank_1_dout3, reg_bank_1_dout4, reg_bank_1_dout5, reg_bank_1_dout6, reg_bank_1_dout7,
       whole_instruction;
  wire [15:12] multiplexer_3_out;

  Clock clock_1 (.out(clk));
  pc_reg pc_reg_1 (.Din(adder_1_out), .PCINC(PCINC), .PCLD(PCLD), .clk(clk), .Dout(pc_reg_1_dout));
  Adder #(.width(12)) adder_1 (.a(pc_reg_1_dout), .b({ALUOP, offset}), .out(adder_1_out));  // open: cin, cout
  RAM #(.addrWidth(12), .dataWidth(16), .bus("separate")) ram_1 (
    .addr(address), .din(Dout), .data({whole_instruction[15], opcode, whole_instruction[11:0]}), .str(MEMLD),
    .clk(clk));  // open: sel, ld, clr
  Multiplexer #(.width(12), .enable("false")) multiplexer_1 (
    .in0(pc_reg_1_dout), .in1(mem_addr), .out(address), .sel(ARMUX));
  control_unit control_unit_1 (
    .address(opcode), .ZF(ZF), .clk(clk), .IRLD(IRLD), .MEMLD(MEMLD), .MUX(MUX), .ZFLD(ZFLD), .REGLD(REGLD),
    .ARMUX(ARMUX), .PCINC(PCINC), .PCLD(PCLD));
  Multiplexer #(.width(16), .enable("false")) multiplexer_2 (
    .in0(alu_rep8_1_res), .in1({whole_instruction[15], opcode, whole_instruction[11:0]}), .out(Din), .sel(MUX));
  Register #(.width(12)) register_1 (
    .D(whole_instruction[11:0]), .en(IRLD), .Q({ALUOP, offset}), .clk(clk));  // open: clr
  Register #(.width(1)) register_2 (.D(alu_rep8_1_zero_flag), .en(ZFLD), .Q(ZF), .clk(clk));  // open: clr
  alu_rep8 alu_rep8_1 (
    .Din1(Dout), .Din2({multiplexer_3_out, mem_addr}), .in_3(ALUOP), .res(alu_rep8_1_res),
    .zero_flag(alu_rep8_1_zero_flag));
  Multiplexer #(.select(3), .width(16), .enable("false")) multiplexer_3 (
    .in0(reg_bank_1_dout0), .in1(reg_bank_1_dout1), .in2(reg_bank_1_dout2), .in3(reg_bank_1_dout3),
    .in4(reg_bank_1_dout4), .in5(reg_bank_1_dout5), .in6(reg_bank_1_dout6), .in7(reg_bank_1_dout7),
    .out({multiplexer_3_out, mem_addr}), .sel(offset[5:3]));
  Multiplexer #(.select(3), .width(16), .enable("false")) multiplexer_4 (
    .in0(reg_bank_1_dout0), .in1(reg_bank_1_dout1), .in2(reg_bank_1_dout2), .in3(reg_bank_1_dout3),
    .in4(reg_bank_1_dout4), .in5(reg_bank_1_dout5), .in6(reg_bank_1_dout6), .in7(reg_bank_1_dout7),
    .out(Dout), .sel(ALUOP[2:0]));
  Hex_Digit_Display hex_digit_display_1 (.value(reg_bank_1_dout0[15:12]));  // open: dp
  Hex_Digit_Display hex_digit_display_2 (.value(reg_bank_1_dout0[11:8]));  // open: dp
  Hex_Digit_Display hex_digit_display_3 (.value(reg_bank_1_dout0[7:4]));  // open: dp
  reg_bank reg_bank_1 (
    .regsel(offset[2:0]), .clk(clk), .Dout0(reg_bank_1_dout0), .Dout1(reg_bank_1_dout1),
    .Dout2(reg_bank_1_dout2), .Dout3(reg_bank_1_dout3), .Dout4(reg_bank_1_dout4), .Dout5(reg_bank_1_dout5),
    .Dout6(reg_bank_1_dout6), .Dout7(reg_bank_1_dout7), .Din(Din), .LD(REGLD));
  Hex_Digit_Display hex_digit_display_4 (.value(reg_bank_1_dout0[3:0]));  // open: dp

  // Other names for the same wires on the sheet: r1[2:0] = offset[2:0]; r3[2:0] = offset[5:3]; offset[11:6] = ALUOP;
  //   r2[2:0] = ALUOP[2:0]; whole_instruction[14:12] = opcode
endmodule

// ALU
module alu_rep8 (
  input  [15:0] Din1,
  input  [15:0] Din2,
  input  [5:0] in_3,
  output [15:0] res,
  output zero_flag
);

  wire [15:0] adder_1_out, adder_2_out, and_1_out, multiplexer_1_out, not_1_out, or_1_out, subtractor_1_out,
       subtractor_2_out, xor_1_out;

  assign not_1_out = ~Din2;  // NOT_Gate not_1, 16 bits wide
  Adder #(.width(16)) adder_1 (.a(Din2), .b(16'h1), .out(adder_1_out));  // open: cin, cout
  Subtractor #(.width(16)) subtractor_1 (.a(Din2), .b(16'h1), .out(subtractor_1_out));  // open: bin, bout
  Adder #(.width(16)) adder_2 (.a(Din1), .b(Din2), .out(adder_2_out));  // open: cin, cout
  Subtractor #(.width(16)) subtractor_2 (.a(Din1), .b(Din2), .out(subtractor_2_out));  // open: bin, bout
  assign and_1_out = Din1 & Din2;  // AND_Gate and_1, 16 bits wide
  assign or_1_out = Din1 | Din1;  // OR_Gate or_1, 16 bits wide
  assign xor_1_out = Din1 ^ Din2;  // XOR_Gate xor_1, 16 bits wide
  Multiplexer #(.select(3), .width(16), .enable("false")) multiplexer_1 (
    .in0(not_1_out), .in1(Din2), .in2(adder_1_out), .in3(subtractor_1_out), .out(multiplexer_1_out),
    .sel(in_3[2:0]));  // open: in4, in5, in6, in7
  Multiplexer #(.select(3), .width(16), .enable("false")) multiplexer_2 (
    .in0(adder_2_out), .in1(subtractor_2_out), .in2(and_1_out), .in3(or_1_out), .in4(xor_1_out),
    .in7(multiplexer_1_out), .out(res), .sel(in_3[5:3]));  // open: in5, in6
  nor nor_1 (zero_flag, res[0], res[1], res[2], res[3], res[4], res[5], res[6], res[7], res[8], res[9], res[10], res[11], res[12], res[13], res[14], res[15]);
endmodule

// pcreg
module pc_reg (
  input  [11:0] Din,
  input  PCINC,
  input  PCLD,
  input  clk,
  output [11:0] Dout
);

  wire and_1_out, and_2_out, not_1_out, or_1_out;
  wire [11:0] adder_1_out, multiplexer_1_out, multiplexer_2_out, subtractor_1_out;

  and and_1 (and_1_out, PCINC, PCLD);
  Multiplexer #(.width(12), .enable("false")) multiplexer_1 (
    .in0(adder_1_out), .in1(subtractor_1_out), .out(multiplexer_1_out), .sel(and_1_out));
  Multiplexer #(.width(12), .enable("false")) multiplexer_2 (
    .in0(multiplexer_1_out), .in1(Din), .out(multiplexer_2_out), .sel(and_2_out));
  and and_2 (and_2_out, not_1_out, PCLD);
  not not_1 (not_1_out, PCINC);
  or or_1 (or_1_out, PCINC, PCLD);
  Register #(.width(12)) register_1 (.D(multiplexer_2_out), .en(or_1_out), .Q(Dout), .clk(clk));  // open: clr
  Subtractor #(.width(12)) subtractor_1 (.a(Dout), .b(12'h1), .out(subtractor_1_out));  // open: bin, bout
  Adder #(.width(12)) adder_1 (.a(Dout), .b(12'h1), .out(adder_1_out));  // open: cin, cout
endmodule

// Control Unit
module control_unit (
  input  [2:0] address,
  input  clk,
  input  ZF,
  output IRLD,
  output MEMLD,
  output MUX,
  output ZFLD,
  output REGLD,
  output ARMUX,
  output PCINC,
  output PCLD
);

  wire [1:1] and_1_out;
  wire [2:0] multiplexer_1_out, multiplexer_2_out, register_1_q;
  wire [8:8] rom_1_data;

  and and_1 (and_1_out[1], ~address[0], ~address[1], address[2]);  // AND_Gate
  Multiplexer #(.select(2), .width(3), .enable("false")) multiplexer_1 (
    .in0(address), .in1(address), .in2(3'b000), .in3(3'b101), .out(multiplexer_1_out),
    .sel({and_1_out[1], ZF}));
  Multiplexer #(.width(3), .enable("false")) multiplexer_2 (
    .in0(3'b000), .in1(multiplexer_1_out), .out(multiplexer_2_out), .sel(rom_1_data[8]));
  Register #(.width(3)) register_1 (.D(multiplexer_2_out), .en(1'b1), .Q(register_1_q), .clk(clk));  // open: clr
  ROM #(.addrWidth(3), .dataWidth(9)) rom_1 (
    .addr(register_1_q), .data({rom_1_data[8], PCLD, PCINC, ARMUX, REGLD, ZFLD, MUX, MEMLD, IRLD}));  // open: sel

  // Notes on the sheet:
  //   contents of rom_1 (hex, n*v repeats v):
  //   141 54 34 22 0 80 0 18
endmodule
