// Logisim project hw2.circ as structural Verilog: 5 circuits, main circuit modified_bird
// Register Bank
module reg_bank (
  input  clk,
  input  [15:0] Din,
  input  LD,
  input  [2:0] regsel,
  input  SP_minus_minus,
  input  SP_plus_plus,
  output [15:0] Dout0,
  output [15:0] Dout1,
  output [15:0] Dout2,
  output [15:0] Dout3,
  output [15:0] Dout4,
  output [15:0] Dout5,
  output [15:0] Dout6,
  output [15:0] Dout7
);

  wire and_1_out, and_2_out, and_3_out, and_4_out, and_5_out, and_6_out, and_7_out, and_8_out, and_9_out,
       and_10_out, decoder_1_out0, decoder_1_out1, decoder_1_out2, decoder_1_out3, decoder_1_out4,
       decoder_1_out5, decoder_1_out6, decoder_1_out7, not_1_out, or_1_out;
  wire [15:0] adder_1_out, multiplexer_1_out, multiplexer_2_out, register_8_q;

  and and_1 (and_1_out, decoder_1_out0, LD);
  and and_2 (and_2_out, decoder_1_out1, LD);
  and and_3 (and_3_out, decoder_1_out2, LD);
  and and_4 (and_4_out, decoder_1_out4, LD);
  and and_5 (and_5_out, decoder_1_out3, LD);
  Decoder #(.select(3), .enable("false")) decoder_1 (
    .out0(decoder_1_out0), .out1(decoder_1_out1), .out2(decoder_1_out2), .out3(decoder_1_out3),
    .out4(decoder_1_out4), .out5(decoder_1_out5), .out6(decoder_1_out6), .out7(decoder_1_out7), .sel(regsel));
  and and_6 (and_6_out, decoder_1_out5, LD);
  and and_7 (and_7_out, decoder_1_out6, LD);
  and and_8 (and_8_out, decoder_1_out7, LD);
  Register #(.width(16)) register_1 (.D(Din), .en(and_1_out), .Q(Dout0), .clk(clk));  // open: clr
  Register #(.width(16)) register_2 (.D(Din), .en(and_2_out), .Q(Dout1), .clk(clk));  // open: clr
  Register #(.width(16)) register_3 (.D(Din), .en(and_3_out), .Q(Dout2), .clk(clk));  // open: clr
  Register #(.width(16)) register_4 (.D(Din), .en(and_5_out), .Q(Dout3), .clk(clk));  // open: clr
  Register #(.width(16)) register_5 (.D(Din), .en(and_4_out), .Q(Dout4), .clk(clk));  // open: clr
  Register #(.width(16)) register_6 (.D(Din), .en(and_6_out), .Q(Dout5), .clk(clk));  // open: clr
  Register #(.width(16)) register_7 (.D(Din), .en(and_7_out), .Q(Dout6), .clk(clk));  // open: clr
  Register #(.width(16)) register_8 (.D(Din), .en(and_8_out), .Q(register_8_q), .clk(clk));  // open: clr
  Register #(.width(16)) register_9 (.D(multiplexer_1_out), .en(or_1_out), .Q(Dout7), .clk(clk));  // open: clr
  Adder #(.width(16)) adder_1 (.a(Dout7), .b(multiplexer_2_out), .out(adder_1_out));  // open: cin, cout
  or or_1 (or_1_out, SP_minus_minus, and_10_out, SP_plus_plus);
  Multiplexer #(.width(16), .enable("false")) multiplexer_1 (
    .in0(adder_1_out), .in1(register_8_q), .out(multiplexer_1_out), .sel(and_10_out));
  not not_1 (not_1_out, SP_plus_plus);
  and and_9 (and_9_out, SP_minus_minus, not_1_out);
  and and_10 (and_10_out, regsel[2], regsel[1], regsel[0]);
  Multiplexer #(.width(16), .enable("false")) multiplexer_2 (
    .in0(16'h1), .in1({16{1'b1}}), .out(multiplexer_2_out), .sel(and_9_out));
endmodule

// ALU
module alu_rep8 (
  input  [15:0] Din1,
  input  [15:0] Din2,
  input  [5:0] in_3,
  output [15:0] res,
  output zero_flag
);

  wire [15:0] adder_1_out, adder_2_out, and_1_out, multiplexer_1_out, not_1_out, or_1_out, subtractor_1_out,
       subtractor_2_out, xor_1_out;

  assign not_1_out = ~Din2;  // NOT_Gate not_1, 16 bits wide
  Adder #(.width(16)) adder_1 (.a(Din2), .b(16'h1), .out(adder_1_out));  // open: cin, cout
  Subtractor #(.width(16)) subtractor_1 (.a(Din2), .b(16'h1), .out(subtractor_1_out));  // open: bin, bout
  Adder #(.width(16)) adder_2 (.a(Din1), .b(Din2), .out(adder_2_out));  // open: cin, cout
  Subtractor #(.width(16)) subtractor_2 (.a(Din1), .b(Din2), .out(subtractor_2_out));  // open: bin, bout
  assign and_1_out = Din1 & Din2;  // AND_Gate and_1, 16 bits wide
  assign or_1_out = Din1 | Din1;  // OR_Gate or_1, 16 bits wide
  assign xor_1_out = Din1 ^ Din2;  // XOR_Gate xor_1, 16 bits wide
  Multiplexer #(.select(3), .width(16), .enable("false")) multiplexer_1 (
    .in0(not_1_out), .in1(Din2), .in2(adder_1_out), .in3(subtractor_1_out), .out(multiplexer_1_out),
    .sel(in_3[2:0]));  // open: in4, in5, in6, in7
  Multiplexer #(.select(3), .width(16), .enable("false")) multiplexer_2 (
    .in0(adder_2_out), .in1(subtractor_2_out), .in2(and_1_out), .in3(or_1_out), .in4(xor_1_out),
    .in7(multiplexer_1_out), .out(res), .sel(in_3[5:3]));  // open: in5, in6
  nor nor_1 (zero_flag, res[0], res[1], res[2], res[3], res[4], res[5], res[6], res[7], res[8], res[9], res[10], res[11], res[12], res[13], res[14], res[15]);
endmodule

// pcreg
module pc_reg (
  input  [15:0] Din,
  input  PCINC,
  input  PCLD,
  input  clk,
  output [15:0] Dout
);

  wire and_1_out, and_2_out, not_1_out, or_1_out;
  wire [15:0] adder_1_out, multiplexer_1_out, multiplexer_2_out, subtractor_1_out;

  and and_1 (and_1_out, PCINC, PCLD);
  Multiplexer #(.width(16), .enable("false")) multiplexer_1 (
    .in0(adder_1_out), .in1(subtractor_1_out), .out(multiplexer_1_out), .sel(and_1_out));
  Multiplexer #(.width(16), .enable("false")) multiplexer_2 (
    .in0(multiplexer_1_out), .in1(Din), .out(multiplexer_2_out), .sel(and_2_out));
  and and_2 (and_2_out, not_1_out, PCLD);
  not not_1 (not_1_out, PCINC);
  or or_1 (or_1_out, PCINC, PCLD);
  Register #(.width(16)) register_1 (.D(multiplexer_2_out), .en(or_1_out), .Q(Dout), .clk(clk));  // open: clr
  Subtractor #(.width(16)) subtractor_1 (.a(Dout), .b(16'h1), .out(subtractor_1_out));  // open: bin, bout
  Adder #(.width(16)) adder_1 (.a(Dout), .b(16'h1), .out(adder_1_out));  // open: cin, cout
endmodule

// Control Unit
module control_unit (
  input  [3:0] address,
  input  clk,
  input  ZF,
  output ARMUX1,
  output PCINC,
  output PCLD,
  output ARMUX0,
  output SP_minus_minus,
  output REGLD,
  output SP_plus_plus,
  output ZFLD,
  output PCMUX,
  output MUX,
  output DATAMUX,
  output MEMLD,
  output IRLD
);

  wire [1:1] and_1_out;
  wire [3:0] multiplexer_1_out, multiplexer_2_out, register_1_q;
  wire [17:0] rom_1_data;

  and and_1 (and_1_out[1], ~address[0], ~address[1], address[2], ~address[3]);  // AND_Gate
  Multiplexer #(.select(2), .width(4), .enable("false")) multiplexer_1 (
    .in0(address), .in1(address), .in2(4'b0000), .in3(4'b0101), .out(multiplexer_1_out),
    .sel({and_1_out[1], ZF}));
  Multiplexer #(.width(4), .enable("false")) multiplexer_2 (
    .in0(rom_1_data[3:0]), .in1(multiplexer_1_out), .out(multiplexer_2_out), .sel(rom_1_data[17]));
  Register #(.width(4)) register_1 (.D(multiplexer_2_out), .en(1'b1), .Q(register_1_q), .clk(clk));  // open: clr
  ROM #(.addrWidth(4), .dataWidth(18)) rom_1 (
    .addr(register_1_q),
    .data({rom_1_data[17], DATAMUX, PCMUX, SP_plus_plus, SP_minus_minus, PCLD, PCINC, ARMUX1, ARMUX0, REGLD, ZFLD, MUX, MEMLD, IRLD, rom_1_data[3:0]}));  // open: sel

  // Notes on the sheet:
  //   contents of rom_1 (hex, n*v repeats v):
  //   20810 940 340 220 0 1000 0 180 2420 400c 13420 400d 540 9400
endmodule

// BIRD
module modified_bird (
  input  [15:0] switchboard_1,
  input  [15:0] switchboard_2
);

  wire alu_rep8_1_zero_flag, and_1_out, and_2_out, and_3_out, and_4_out, and_5_out, and_6_out, and_7_out,
       ARMUX0, ARMUX1, clk, DATAMUX, disp_out, IRLD, MEMWT, MUX, pb1_out_2, pb2_out_2, PCINC, PCLD, PCMUX,
       push_button_1_out, push_button_2_out, REGLD, sb1_out_2, sb2_out_2, SP_minus_minus, SP_plus_plus, ZF,
       ZFLD;
  wire [0:0] pb1_out, pb2_out;
  wire [5:0] ALUOP, offset;
  wire [11:0] negator_1_out;
  wire [15:0] adder_1_out, address, alu_rep8_1_res, DataIn, DataOut, Din, Dout, mem_addr, MemDin,
       multiplexer_1_out, multiplexer_3_out, multiplexer_4_out, multiplexer_6_out, multiplexer_8_out,
       multiplexer_9_out, pc_reg_1_dout, reg_bank_1_dout0, reg_bank_1_dout1, reg_bank_1_dout2,
       reg_bank_1_dout3, reg_bank_1_dout4, reg_bank_1_dout5, reg_bank_1_dout6, SP, SSEG_DATA,
       subtractor_1_out;

  Multiplexer #(.width(16), .enable("false")) multiplexer_1 (
    .in0(multiplexer_3_out), .in1(Din), .out(multiplexer_1_out), .sel(PCMUX));
  Negator #(.width(12)) negator_1 (.in({ALUOP, offset}), .out(negator_1_out));
  Clock clock_1 (.out(clk));
  pc_reg pc_reg_1 (.Din(multiplexer_1_out), .PCINC(PCINC), .PCLD(PCLD), .clk(clk), .Dout(pc_reg_1_dout));
  Adder #(.width(16)) adder_1 (.a(pc_reg_1_dout), .b({4'b0000, ALUOP, offset}), .out(adder_1_out));  // open: cin, cout
  Subtractor #(.width(16)) subtractor_1 (
    .a(pc_reg_1_dout), .b({4'b0000, negator_1_out}), .out(subtractor_1_out));  // open: bin, bout
  and and_1 (and_1_out, disp_out, MEMWT);
  and disp (disp_out, ~address[15], address[14], address[13], ~address[12], ~address[11], ~address[10], ~address[9], ~address[8], ~address[7], ~address[6], ~address[5], ~address[4], ~address[3], address[2], ~address[1], ~address[0]);  // AND_Gate
  Multiplexer #(.width(16), .enable("false")) multiplexer_2 (
    .in0(Dout), .in1(pc_reg_1_dout), .out(DataOut), .sel(DATAMUX));
  Multiplexer #(.width(16), .enable("false")) multiplexer_3 (
    .in0(adder_1_out), .in1(subtractor_1_out), .out(multiplexer_3_out), .sel(ALUOP[5]));
  Register #(.width(16)) register_1 (.D(DataOut), .en(and_1_out), .Q(SSEG_DATA), .clk(clk));  // open: clr
  Multiplexer #(.width(16), .enable("false")) multiplexer_4 (
    .in0({16{1'b0}}), .in1({{15{1'b0}}, pb2_out[0]}), .out(multiplexer_4_out), .sel(pb2_out_2));
  Button push_button_1 (.out(push_button_1_out));
  and pb2 (pb2_out_2, ~address[15], address[14], address[13], ~address[12], ~address[11], ~address[10], ~address[9], ~address[8], ~address[7], ~address[6], ~address[5], ~address[4], ~address[3], ~address[2], address[1], address[0]);  // AND_Gate
  and and_2 (and_2_out, ~pb1_out[0], push_button_1_out);  // AND_Gate
  Multiplexer #(.select(2), .width(16), .enable("false")) multiplexer_5 (
    .in0(pc_reg_1_dout), .in1(mem_addr), .in2(SP), .out(address), .sel({ARMUX1, ARMUX0}));  // open: in3
  Multiplexer #(.width(16), .enable("false")) multiplexer_6 (
    .in0(multiplexer_4_out), .in1({{15{1'b0}}, pb1_out[0]}), .out(multiplexer_6_out), .sel(pb1_out_2));
  Register #(.width(1)) register_2 (.D(and_2_out), .en(and_2_out), .Q(pb1_out[0]), .clk(clk), .clr(and_3_out));
  control_unit control_unit_1 (
    .address(Din[15:12]), .DATAMUX(DATAMUX), .PCMUX(PCMUX), .SP_plus_plus(SP_plus_plus),
    .SP_minus_minus(SP_minus_minus), .PCLD(PCLD), .PCINC(PCINC), .ZF(ZF), .clk(clk), .ARMUX1(ARMUX1),
    .ARMUX0(ARMUX0), .REGLD(REGLD), .ZFLD(ZFLD), .MUX(MUX), .MEMLD(MEMWT), .IRLD(IRLD));
  Multiplexer #(.width(16), .enable("false")) multiplexer_7 (
    .in0(MemDin), .in1(multiplexer_8_out), .out(Din), .sel(and_4_out));
  Multiplexer #(.width(16), .enable("false")) multiplexer_8 (
    .in0(multiplexer_9_out), .in1(switchboard_1), .out(multiplexer_8_out), .sel(sb1_out_2));
  Multiplexer #(.width(16), .enable("false")) multiplexer_9 (
    .in0(multiplexer_6_out), .in1(switchboard_2), .out(multiplexer_9_out), .sel(sb2_out_2));
  and pb1 (pb1_out_2, ~address[15], address[14], address[13], ~address[12], ~address[11], ~address[10], ~address[9], ~address[8], ~address[7], ~address[6], ~address[5], ~address[4], ~address[3], ~address[2], address[1], ~address[0]);  // AND_Gate
  and and_3 (and_3_out, disp_out, pb1_out[0]);
  Multiplexer #(.width(16), .enable("false")) multiplexer_10 (.in0(alu_rep8_1_res), .in1(Din), .out(DataIn), .sel(MUX));
  Register #(.width(12)) register_3 (.D(Din[11:0]), .en(IRLD), .Q({ALUOP, offset}), .clk(clk));  // open: clr
  and sb2 (sb2_out_2, ~address[15], address[14], address[13], ~address[12], ~address[11], ~address[10], ~address[9], ~address[8], ~address[7], ~address[6], ~address[5], ~address[4], ~address[3], ~address[2], ~address[1], address[0]);  // AND_Gate
  Button push_button_2 (.out(push_button_2_out));
  Register #(.width(1)) register_4 (.D(alu_rep8_1_zero_flag), .en(ZFLD), .Q(ZF), .clk(clk));  // open: clr
  and and_4 (and_4_out, ~address[12], address[13], address[14], ~address[15]);  // AND_Gate
  and and_5 (and_5_out, ~pb2_out[0], push_button_2_out);  // AND_Gate
  alu_rep8 alu_rep8_1 (
    .Din1(Dout), .Din2(mem_addr), .in_3(ALUOP), .res(alu_rep8_1_res), .zero_flag(alu_rep8_1_zero_flag));
  and sb1 (sb1_out_2, ~address[15], address[14], address[13], ~address[12], ~address[11], ~address[10], ~address[9], ~address[8], ~address[7], ~address[6], ~address[5], ~address[4], ~address[3], ~address[2], ~address[1], ~address[0]);  // AND_Gate
  Register #(.width(1)) register_5 (.D(and_5_out), .en(and_5_out), .Q(pb2_out[0]), .clk(clk), .clr(and_6_out));
  Multiplexer #(.select(3), .width(16), .enable("false")) multiplexer_11 (
    .in0(reg_bank_1_dout0), .in1(reg_bank_1_dout1), .in2(reg_bank_1_dout2), .in3(reg_bank_1_dout3),
    .in4(reg_bank_1_dout4), .in5(reg_bank_1_dout5), .in6(reg_bank_1_dout6), .in7(SP), .out(mem_addr),
    .sel(offset[5:3]));
  Multiplexer #(.select(3), .width(16), .enable("false")) multiplexer_12 (
    .in0(reg_bank_1_dout0), .in1(reg_bank_1_dout1), .in2(reg_bank_1_dout2), .in3(reg_bank_1_dout3),
    .in4(reg_bank_1_dout4), .in5(reg_bank_1_dout5), .in6(reg_bank_1_dout6), .in7(SP), .out(Dout),
    .sel(ALUOP[2:0]));
  and and_6 (and_6_out, disp_out, pb2_out[0]);
  and and_7 (and_7_out, ~address[15], MEMWT);  // AND_Gate
  RAM #(.addrWidth(16), .dataWidth(16), .bus("separate")) ram_1 (
    .addr(address), .din(DataOut), .data(MemDin), .str(and_7_out), .clk(clk));  // open: sel, ld, clr
  Hex_Digit_Display hex_digit_display_1 (.value(SSEG_DATA[15:12]));  // open: dp
  Hex_Digit_Display hex_digit_display_2 (.value(SSEG_DATA[11:8]));  // open: dp
  reg_bank reg_bank_1 (
    .regsel(offset[2:0]), .clk(clk), .SP_minus_minus(SP_minus_minus), .SP_plus_plus(SP_plus_plus),
    .Dout0(reg_bank_1_dout0), .Dout1(reg_bank_1_dout1), .Dout2(reg_bank_1_dout2), .Dout3(reg_bank_1_dout3),
    .Dout4(reg_bank_1_dout4), .Dout5(reg_bank_1_dout5), .Dout6(reg_bank_1_dout6), .Dout7(SP), .Din(DataIn),
    .LD(REGLD));
  Hex_Digit_Display hex_digit_display_3 (.value(SSEG_DATA[7:4]));  // open: dp
  Hex_Digit_Display hex_digit_display_4 (.value(SSEG_DATA[3:0]));  // open: dp

  // Other names for the same wires on the sheet: r1[2:0] = offset[2:0]; r3[2:0] = offset[5:3]; offset[11:6] = ALUOP;
  //   r2[2:0] = ALUOP[2:0]; OPCODE[3:0] = Din[15:12]; sb1_out[15:0] = switchboard_1; sb2_out[15:0] = switchboard_2
endmodule
