// Logisim project hw3.circ as structural Verilog: 6 circuits, main circuit modified_vertebrate
// Register Bank
module reg_bank (
  input  clk,
  input  STI,
  input  CLI,
  input  ZFSET,
  input  Z,
  input  FLAGWT,
  input  [15:0] Din,
  input  LD,
  input  [2:0] regsel,
  input  SP_minus_minus,
  input  SP_plus_plus,
  output IF,
  output [15:0] Dout0,
  output [15:0] Dout1,
  output [15:0] Dout2,
  output [15:0] Dout3,
  output [15:0] Dout4,
  output ZF,
  output [15:0] Dout5,
  output [15:0] Dout7
);

  wire and_1_out, and_2_out, and_3_out, and_4_out, and_5_out, and_6_out, and_7_out, and_8_out, and_9_out,
       and_10_out, and_11_out, and_12_out, and_13_out, and_15_out, and_16_out, decoder_1_out0,
       decoder_1_out1, decoder_1_out2, decoder_1_out3, decoder_1_out4, decoder_1_out5, decoder_1_out6,
       decoder_1_out7, not_1_out, or_1_out, or_2_out, or_3_out, or_4_out, or_5_out;
  wire [15:0] adder_1_out, multiplexer_1_out, multiplexer_2_out, register_9_q;

  and and_1 (and_1_out, ~Din[0], FLAGWT);  // AND_Gate
  and and_2 (and_2_out, Din[1], FLAGWT);
  and and_3 (and_3_out, ~Din[1], FLAGWT);  // AND_Gate
  and and_4 (and_4_out, Din[0], FLAGWT);
  and and_5 (and_5_out, Z, ZFSET);
  or or_1 (or_1_out, and_3_out, CLI);
  or or_2 (or_2_out, and_4_out, and_5_out);
  or or_3 (or_3_out, and_2_out, STI);
  or or_4 (or_4_out, and_1_out, and_6_out);
  and and_6 (and_6_out, ~Z, ZFSET);  // AND_Gate
  Register #(.width(1)) register_1 (.D(or_3_out), .en(or_3_out), .Q(IF), .clk(clk), .clr(or_1_out));
  Register #(.width(1)) register_2 (.D(or_2_out), .en(or_2_out), .Q(ZF), .clk(clk), .clr(or_4_out));
  and and_7 (and_7_out, decoder_1_out0, LD);
  and and_8 (and_8_out, decoder_1_out1, LD);
  and and_9 (and_9_out, decoder_1_out2, LD);
  and and_10 (and_10_out, decoder_1_out3, LD);
  Decoder #(.select(3), .enable("false")) decoder_1 (
    .out0(decoder_1_out0), .out1(decoder_1_out1), .out2(decoder_1_out2), .out3(decoder_1_out3),
    .out4(decoder_1_out4), .out5(decoder_1_out5), .out6(decoder_1_out6), .out7(decoder_1_out7), .sel(regsel));
  and and_11 (and_11_out, decoder_1_out4, LD);
  and and_12 (and_12_out, decoder_1_out5, LD);
  and and_13 (and_13_out, decoder_1_out7, LD);
  // AND_Gate and_14 has open pins: in0=decoder_1_out6, in1=LD, out=open
  Register #(.width(16)) register_3 (.D(Din), .en(and_7_out), .Q(Dout0), .clk(clk));  // open: clr
  Register #(.width(16)) register_4 (.D(Din), .en(and_8_out), .Q(Dout1), .clk(clk));  // open: clr
  Register #(.width(16)) register_5 (.D(Din), .en(and_9_out), .Q(Dout2), .clk(clk));  // open: clr
  Register #(.width(16)) register_6 (.D(Din), .en(and_10_out), .Q(Dout3), .clk(clk));  // open: clr
  Register #(.width(16)) register_7 (.D(Din), .en(and_11_out), .Q(Dout4), .clk(clk));  // open: clr
  Register #(.width(16)) register_8 (.D(Din), .en(and_12_out), .Q(Dout5), .clk(clk));  // open: clr
  Register #(.width(16)) register_9 (.D(Din), .en(and_13_out), .Q(register_9_q), .clk(clk));  // open: clr
  Adder #(.width(16)) adder_1 (.a(Dout7), .b(multiplexer_2_out), .out(adder_1_out));  // open: cin, cout
  Register #(.width(16)) register_10 (.D(multiplexer_1_out), .en(or_5_out), .Q(Dout7), .clk(clk));  // open: clr
  or or_5 (or_5_out, SP_minus_minus, and_16_out, SP_plus_plus);
  not not_1 (not_1_out, SP_plus_plus);
  Multiplexer #(.width(16), .enable("false")) multiplexer_1 (
    .in0(adder_1_out), .in1(register_9_q), .out(multiplexer_1_out), .sel(and_16_out));
  and and_15 (and_15_out, SP_minus_minus, not_1_out);
  and and_16 (and_16_out, regsel[2], regsel[1], regsel[0]);
  Multiplexer #(.width(16), .enable("false")) multiplexer_2 (
    .in0(16'h1), .in1({16{1'b1}}), .out(multiplexer_2_out), .sel(and_15_out));
endmodule

// ALU
module alu_rep8 (
  input  [15:0] Din1,
  input  [15:0] Din2,
  input  [5:0] in_3,
  output [15:0] res,
  output zero_flag
);

  wire [15:0] adder_1_out, adder_2_out, and_1_out, multiplexer_1_out, not_1_out, or_1_out, subtractor_1_out,
       subtractor_2_out, xor_1_out;

  assign not_1_out = ~Din2;  // NOT_Gate not_1, 16 bits wide
  Adder #(.width(16)) adder_1 (.a(Din2), .b(16'h1), .out(adder_1_out));  // open: cin, cout
  Subtractor #(.width(16)) subtractor_1 (.a(Din2), .b(16'h1), .out(subtractor_1_out));  // open: bin, bout
  Adder #(.width(16)) adder_2 (.a(Din1), .b(Din2), .out(adder_2_out));  // open: cin, cout
  Subtractor #(.width(16)) subtractor_2 (.a(Din1), .b(Din2), .out(subtractor_2_out));  // open: bin, bout
  assign and_1_out = Din1 & Din2;  // AND_Gate and_1, 16 bits wide
  assign or_1_out = Din1 | Din1;  // OR_Gate or_1, 16 bits wide
  assign xor_1_out = Din1 ^ Din2;  // XOR_Gate xor_1, 16 bits wide
  Multiplexer #(.select(3), .width(16), .enable("false")) multiplexer_1 (
    .in0(not_1_out), .in1(Din2), .in2(adder_1_out), .in3(subtractor_1_out), .out(multiplexer_1_out),
    .sel(in_3[2:0]));  // open: in4, in5, in6, in7
  Multiplexer #(.select(3), .width(16), .enable("false")) multiplexer_2 (
    .in0(adder_2_out), .in1(subtractor_2_out), .in2(and_1_out), .in3(or_1_out), .in4(xor_1_out),
    .in7(multiplexer_1_out), .out(res), .sel(in_3[5:3]));  // open: in5, in6
  nor nor_1 (zero_flag, res[0], res[1], res[2], res[3], res[4], res[5], res[6], res[7], res[8], res[9], res[10], res[11], res[12], res[13], res[14], res[15]);
endmodule

// pcreg
module pc_reg (
  input  [15:0] Din,
  input  PCINC,
  input  PCLD,
  input  clk,
  output [15:0] Dout
);

  wire and_1_out, and_2_out, not_1_out, or_1_out;
  wire [15:0] adder_1_out, multiplexer_1_out, multiplexer_2_out, subtractor_1_out;

  and and_1 (and_1_out, PCINC, PCLD);
  Multiplexer #(.width(16), .enable("false")) multiplexer_1 (
    .in0(adder_1_out), .in1(subtractor_1_out), .out(multiplexer_1_out), .sel(and_1_out));
  Multiplexer #(.width(16), .enable("false")) multiplexer_2 (
    .in0(multiplexer_1_out), .in1(Din), .out(multiplexer_2_out), .sel(and_2_out));
  and and_2 (and_2_out, not_1_out, PCLD);
  not not_1 (not_1_out, PCINC);
  or or_1 (or_1_out, PCINC, PCLD);
  Register #(.width(16)) register_1 (.D(multiplexer_2_out), .en(or_1_out), .Q(Dout), .clk(clk));  // open: clr
  Subtractor #(.width(16)) subtractor_1 (.a(Dout), .b(16'h1), .out(subtractor_1_out));  // open: bin, bout
  Adder #(.width(16)) adder_1 (.a(Dout), .b(16'h1), .out(adder_1_out));  // open: cin, cout
endmodule

// Control Unit
module control_unit (
  input  [3:0] address,
  input  clk,
  input  ZF,
  input  INT,
  input  INTFLAG,
  output ARMUX1,
  output ARMUX0,
  output MEMLD,
  output DATAMUX1,
  output PCINC,
  output DATAMUX0,
  output PCLD,
  output PCMUX,
  output ZFLD,
  output FLAGWT,
  output IRLD,
  output STI,
  output SP_plus_plus,
  output CLI,
  output SP_minus_minus,
  output INTACK,
  output REGLD,
  output INTLD,
  output MUX
);

  wire and_2_out, and_3_out;
  wire [1:1] and_1_out;
  wire [3:0] multiplexer_1_out;
  wire [4:0] multiplexer_2_out, multiplexer_3_out, register_1_q, rom_1_data_2;
  wire [24:24] rom_1_data;

  and and_1 (and_1_out[1], ~address[0], ~address[1], address[2], ~address[3]);  // AND_Gate
  Multiplexer #(.select(2), .width(4), .enable("false")) multiplexer_1 (
    .in0(address), .in1(address), .in2(4'b0000), .in3(4'b0101), .out(multiplexer_1_out),
    .sel({and_1_out[1], ZF}));
  Multiplexer #(.width(5), .enable("false")) multiplexer_2 (
    .in0(rom_1_data_2), .in1({1'b0, multiplexer_1_out}), .out(multiplexer_2_out), .sel(rom_1_data[24]));
  Multiplexer #(.width(5), .enable("false")) multiplexer_3 (
    .in0(multiplexer_2_out), .in1(5'b10101), .out(multiplexer_3_out), .sel(and_2_out));
  and and_2 (and_2_out, INT, INTFLAG, and_3_out);
  Register #(.width(5)) register_1 (.D(multiplexer_3_out), .en(1'b1), .Q(register_1_q), .clk(clk));  // open: clr
  ROM #(.addrWidth(5), .dataWidth(25)) rom_1 (
    .addr(register_1_q),
    .data({rom_1_data[24], MUX, REGLD, SP_minus_minus, SP_plus_plus, IRLD, ZFLD, PCLD, PCINC, ARMUX1, ARMUX0, MEMLD, DATAMUX1, DATAMUX0, PCMUX, FLAGWT, STI, CLI, INTACK, INTLD, rom_1_data_2}));  // open: sel
  and and_3 (and_3_out, ~rom_1_data_2[4], ~rom_1_data_2[3], ~rom_1_data_2[2], ~rom_1_data_2[1], ~rom_1_data_2[0]);  // AND_Gate

  // Notes on the sheet:
  //   contents of rom_1 (hex, n*v repeats v):
  //   1090000 c10000 c04000 6000 0 80018 0 440000 20a000 100012 28a814 100013 100 80 100010 0 908211 28500
  //   c08000 28400 20000 20a896 20b077 2c500 20000
endmodule

module PIC (
  input  dev0,
  output Int,
  output [15:0] IntVec
);

  wire priority_encoder_1_p2;

  not not_1 (Int, priority_encoder_1_p2);
  // Priority_Encoder #(.disabled(0)) priority_encoder_1: pin names not known; wires that end beside it: IntVec[2:0], priority_encoder_1_p2, dev0, 1'b0, 1'b0, 1'b0, 1'b0, 1'b0, 1'b0, 1'b0

  assign IntVec[15:3] = {13{1'b0}};
endmodule

module modified_vertebrate (
  input  [15:0] switchboard_1,
  input  [15:0] switchboard_2
);

  wire and_1_out, and_2_out, and_3_out, and_4_out, and_5_out, and_6_out, and_7_out, ARMUX0, ARMUX1, CLI, clk,
       DATAMUX0, DATAMUX1, dev_timer, disp_out, FLAGWT, IF, INT, INTACK, INTLD, IRLD, MEMWT, MUX, not_1_out,
       pb1_out_2, PCINC, PCLD, PCMUX, push_button_out, REGLD, sb1_out_2, sb2_out_2, SP_minus_minus,
       SP_plus_plus, STI, timer, Z, ZF, ZFLD;
  wire [0:0] pb1_out;
  wire [2:0] r1, r3;
  wire [3:0] register_5_q_2, register_5_q_3;
  wire [5:0] ALUOP;
  wire [7:0] register_5_q;
  wire [15:0] adder_1_out, adder_2_out, adder_3_out, address, alu_rep8_1_res, DataIn, DataOut, Din, Dout,
       IDT, mem_addr, MemDin, multiplexer_1_out, multiplexer_3_out, multiplexer_5_out, multiplexer_7_out,
       multiplexer_8_out, multiplexer_9_out, negator_1_out, pc_reg_1_dout, pic_1_intvec, reg_bank_1_dout0,
       reg_bank_1_dout1, reg_bank_1_dout2, reg_bank_1_dout3, reg_bank_1_dout4, reg_bank_1_dout5,
       register_4_q, SP, SSEG_DATA, subtractor_1_out;

  Multiplexer #(.width(16), .enable("false")) multiplexer_1 (
    .in0(multiplexer_3_out), .in1(Din), .out(multiplexer_1_out), .sel(PCMUX));
  Negator #(.width(16)) negator_1 (.in(Din), .out(negator_1_out));
  Clock clock_1 (.out(clk));
  Adder #(.width(16)) adder_1 (.a(pc_reg_1_dout), .b(Din), .out(adder_1_out));  // open: cin, cout
  Subtractor #(.width(16)) subtractor_1 (
    .a(pc_reg_1_dout), .b(negator_1_out), .out(subtractor_1_out));  // open: bin, bout
  and and_1 (and_1_out, disp_out, MEMWT);
  and disp (disp_out, ~address[15], address[14], address[13], ~address[12], ~address[11], ~address[10], ~address[9], ~address[8], ~address[7], ~address[6], ~address[5], ~address[4], ~address[3], address[2], ~address[1], ~address[0]);  // AND_Gate
  Multiplexer #(.select(2), .width(16), .enable("false")) multiplexer_2 (
    .in0(Dout), .in1(pc_reg_1_dout), .in2({{14{1'b0}}, IF, ZF}), .out(DataOut), .sel({DATAMUX1, DATAMUX0}));  // open: in3
  pc_reg pc_reg_1 (.Din(multiplexer_1_out), .PCINC(PCINC), .PCLD(PCLD), .clk(clk), .Dout(pc_reg_1_dout));
  Multiplexer #(.width(16), .enable("false")) multiplexer_3 (
    .in0(adder_1_out), .in1(subtractor_1_out), .out(multiplexer_3_out), .sel(Din[15]));
  Register #(.width(16)) register_1 (.D(DataOut), .en(and_1_out), .Q(SSEG_DATA), .clk(clk));  // open: clr
  Button push_button (.out(push_button_out));
  Register #(.width(16)) register_2 (.D(adder_2_out), .en(INTLD), .Q(IDT), .clk(clk));  // open: clr
  Adder #(.width(16)) adder_2 (.a(Din), .b(16'h7f0), .out(adder_2_out));  // open: cin, cout
  and u_timer (timer, ~address[15], address[14], address[13], ~address[12], ~address[11], ~address[10], ~address[9], ~address[8], ~address[7], ~address[6], ~address[5], ~address[4], ~address[3], ~address[2], address[1], address[0]);  // AND_Gate
  and and_2 (and_2_out, ~pb1_out[0], push_button_out);  // AND_Gate
  Multiplexer #(.select(2), .width(16), .enable("false")) multiplexer_4 (
    .in0(pc_reg_1_dout), .in1(mem_addr), .in2(SP), .in3(IDT), .out(address), .sel({ARMUX1, ARMUX0}));
  Multiplexer #(.width(16), .enable("false")) multiplexer_5 (
    .in0({16{1'b0}}), .in1({{15{1'b0}}, pb1_out[0]}), .out(multiplexer_5_out), .sel(pb1_out_2));
  S_R_Flip_Flop s_r_ff_1 (.S(and_2_out), .clk(clk), .R(and_3_out), .Q(pb1_out[0]));  // open: Qn, preset, reset, en
  control_unit control_unit_1 (
    .PCINC(PCINC), .PCLD(PCLD), .ZFLD(ZFLD), .IRLD(IRLD), .SP_plus_plus(SP_plus_plus),
    .SP_minus_minus(SP_minus_minus), .REGLD(REGLD), .MUX(MUX), .address(Din[15:12]), .ARMUX1(ARMUX1),
    .ARMUX0(ARMUX0), .MEMLD(MEMWT), .ZF(ZF), .INT(INT), .INTFLAG(IF), .clk(clk), .DATAMUX1(DATAMUX1),
    .DATAMUX0(DATAMUX0), .PCMUX(PCMUX), .FLAGWT(FLAGWT), .STI(STI), .CLI(CLI), .INTACK(INTACK), .INTLD(INTLD));
  Multiplexer #(.width(16), .enable("false")) multiplexer_6 (
    .in0(multiplexer_7_out), .in1(pic_1_intvec), .out(Din), .sel(INTACK));
  Multiplexer #(.width(16), .enable("false")) multiplexer_7 (
    .in0(MemDin), .in1(multiplexer_9_out), .out(multiplexer_7_out), .sel(and_4_out));
  Multiplexer #(.width(16), .enable("false")) multiplexer_8 (
    .in0(multiplexer_5_out), .in1(switchboard_2), .out(multiplexer_8_out), .sel(sb2_out_2));
  and and_3 (and_3_out, sb2_out_2, pb1_out[0]);
  Multiplexer #(.width(16), .enable("false")) multiplexer_9 (
    .in0(multiplexer_8_out), .in1(switchboard_1), .out(multiplexer_9_out), .sel(sb1_out_2));
  and pb1 (pb1_out_2, ~address[15], address[14], address[13], ~address[12], ~address[11], ~address[10], ~address[9], ~address[8], ~address[7], ~address[6], ~address[5], ~address[4], ~address[3], ~address[2], address[1], ~address[0]);  // AND_Gate
  PIC pic_1 (.IntVec(pic_1_intvec), .Int(INT), .dev0(dev_timer));
  Multiplexer #(.width(16), .enable("false")) multiplexer_10 (.in0(alu_rep8_1_res), .in1(Din), .out(DataIn), .sel(MUX));
  Register #(.width(12)) register_3 (.D(Din[11:0]), .en(IRLD), .Q({ALUOP, r3, r1}), .clk(clk));  // open: clr
  and sb2 (sb2_out_2, ~address[15], address[14], address[13], ~address[12], ~address[11], ~address[10], ~address[9], ~address[8], ~address[7], ~address[6], ~address[5], ~address[4], ~address[3], ~address[2], ~address[1], address[0]);  // AND_Gate
  Hex_Digit_Display hex_digit_display_1 (.value(SSEG_DATA[15:12]));  // open: dp
  and and_4 (and_4_out, ~address[12], address[13], address[14], ~address[15]);  // AND_Gate
  Hex_Digit_Display hex_digit_display_2 (.value(SSEG_DATA[11:8]));  // open: dp
  alu_rep8 alu_rep8_1 (.Din1(Dout), .Din2(mem_addr), .in_3(ALUOP), .res(alu_rep8_1_res), .zero_flag(Z));
  and sb1 (sb1_out_2, ~address[15], address[14], address[13], ~address[12], ~address[11], ~address[10], ~address[9], ~address[8], ~address[7], ~address[6], ~address[5], ~address[4], ~address[3], ~address[2], ~address[1], ~address[0]);  // AND_Gate
  Hex_Digit_Display hex_digit_display_3 (.value(SSEG_DATA[3:0]));  // open: dp
  Hex_Digit_Display hex_digit_display_4 (.value(SSEG_DATA[7:4]));  // open: dp
  Multiplexer #(.select(3), .width(16), .enable("false")) multiplexer_11 (
    .in0(reg_bank_1_dout0), .in1(reg_bank_1_dout1), .in2(reg_bank_1_dout2), .in3(reg_bank_1_dout3),
    .in4(reg_bank_1_dout4), .in5(reg_bank_1_dout5), .in7(SP), .out(mem_addr), .sel(r3));  // open: in6
  Multiplexer #(.select(3), .width(16), .enable("false")) multiplexer_12 (
    .in0(reg_bank_1_dout0), .in1(reg_bank_1_dout1), .in2(reg_bank_1_dout2), .in3(reg_bank_1_dout3),
    .in4(reg_bank_1_dout4), .in5(reg_bank_1_dout5), .in7(SP), .out(Dout), .sel(ALUOP[2:0]));  // open: in6
  and and_5 (and_5_out, ~address[15], MEMWT);  // AND_Gate
  RAM #(.addrWidth(16), .dataWidth(16), .bus("separate")) ram_1 (
    .addr(address), .din(DataOut), .data(MemDin), .str(and_5_out), .clk(clk));  // open: sel, ld, clr
  Hex_Digit_Display hex_digit_display_5 (.value(register_5_q_3));  // open: dp
  Adder #(.width(16)) adder_3 (.a(register_4_q), .b(16'h1), .out(adder_3_out));  // open: cin, cout
  not not_1 (not_1_out, dev_timer);
  Hex_Digit_Display hex_digit_display_6 (.value(register_5_q_2));  // open: dp
  Register #(.width(16)) register_4 (.D(adder_3_out), .en(not_1_out), .Q(register_4_q), .clk(clk), .clr(and_7_out));
  Hex_Digit_Display hex_digit_display_7 (.value(register_5_q[3:0]));  // open: dp
  Hex_Digit_Display hex_digit_display_8 (.value(register_5_q[7:4]));  // open: dp
  and and_6 (and_6_out, timer, MEMWT);
  reg_bank reg_bank_1 (
    .regsel(r1), .clk(clk), .STI(STI), .FLAGWT(FLAGWT), .CLI(CLI), .SP_minus_minus(SP_minus_minus),
    .SP_plus_plus(SP_plus_plus), .IF(IF), .Dout0(reg_bank_1_dout0), .Dout1(reg_bank_1_dout1),
    .Dout2(reg_bank_1_dout2), .Dout3(reg_bank_1_dout3), .Dout4(reg_bank_1_dout4), .ZF(ZF),
    .Dout5(reg_bank_1_dout5), .ZFSET(ZFLD), .Z(Z), .Dout7(SP), .Din(DataIn), .LD(REGLD));
  and and_7 (and_7_out, address[0], ~address[1], ~address[2], ~address[3], ~address[4], ~address[5], ~address[6], address[7], ~address[8], ~address[9], ~address[10], ~address[11]);  // AND_Gate
  Register #(.width(16)) register_5 (
    .D(DataOut), .en(and_6_out), .Q({register_5_q_3, register_5_q_2, register_5_q}), .clk(clk));  // open: clr
  and and_8 (dev_timer, ~register_4_q[0], ~register_4_q[1], ~register_4_q[2], ~register_4_q[3], ~register_4_q[4], ~register_4_q[5], ~register_4_q[6], ~register_4_q[7], ~register_4_q[8], ~register_4_q[9], ~register_4_q[10], register_4_q[11], ~register_4_q[12], ~register_4_q[13], ~register_4_q[14], ~register_4_q[15]);  // AND_Gate

  // Other names for the same wires on the sheet: r2[2:0] = ALUOP[2:0]; isr_addr[15:0] = address; offset[15:0] = Din;
  //   OPCODE[3:0] = Din[15:12]; sb1_out[15:0] = switchboard_1; sb2_out[15:0] = switchboard_2
endmodule
